# Fritzing sketch buttons (saved by Fritzing 1.0.0d)

parts:
  Mod2 = Raspberry Pi Pico
  S4 = Momentary Switch [package=ksa_sealed_tac_switch]
  S5 = Momentary Switch [package=ksa_sealed_tac_switch]
  S6 = Momentary Switch [package=ksa_sealed_tac_switch]

nets:
  N1: Mod2.pin_1, S5.2
  N2: Mod2.pin_2, S6.2
  N3: Mod2.pin_4, S4.2
  N4: Mod2.pin_36, S4.4, S5.4, S6.4

custom parts:
  Raspberry Pi Pico: Raspberry Pi Pico. Based around the RP2040 microcontroller the Pico is a low cost microcontroller device bringing Raspberry Pi quality, cost, and easy of use to the microcontroller space. Jan 2021, Split part in to two versions: tht (this one) and SMD. This one will drill holes for a .1 in header in pcb to allow plugging in the module as well as providing pads to solder the module to the top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
