# Fritzing sketch display (saved by Fritzing 1.0.2b)
breadboards: 1

parts:
  PICO = Raspberry Pi Pico W
  DISPLAY = OLED 0.96" 128x64 I2C SSD1306

nets:
  N1: PICO.pin_23, PICO.pin_33, DISPLAY.GND
  N2: PICO.pin_24, DISPLAY.SCA
  N3: PICO.pin_25, DISPLAY.SCL
  N4: PICO.pin_36, DISPLAY.VCC

notes:
  ssd1306 or sh1106

custom parts:
  Raspberry Pi Pico W: Raspberry Pi Pico W. Based around the RP2040 microcontroller the Pico W is a low cost microcontroller device bringing Raspberry Pi quality, cost, and easy of use to the microcontroller space. The areas marked KEEPOUT in pcb silkscreen should not have traces running through them to avoid shorts on a soldered in module!
